# Fritzing sketch WiringDiagram20180415 (saved by Fritzing 0.9.3b)
breadboards: 1

parts:
  Part1 = Arduino Uno (Rev3)
  LED1 = RGB LED (com. cathode, rgb) [package="5 mm [THT]"]
  LED2 = LED - 5mm [color="Red (633nm)" package="5 mm [THT]"]

nets:
  N1: Part1.D11_PWM/MOSI, LED2.cathode
  N2: Part1.GND, LED1.common_cathode, LED2.anode
  N3: Part1.D3_PWM, LED1.blue_anode
  N4: Part1.D5_PWM, LED1.green_anode
  N5: Part1.D6_PWM, LED1.red_anode
